// Logisim project proj.circ as structural Verilog: 7 circuits, main circuit main
module main (
  output [15:0] out_1
);

  wire ALU_zero, and_1_out, clock_1_out, clock_2_out, clock_3_out, Control_alusrc, Control_branch,
       Control_jump, Control_memread, Control_memtoreg, Control_memwrite, Control_regdst, Control_regwrite;
  wire [1:0] Control_alu_control;
  wire [3:0] adder_1_out, adder_2_out, ALU_alu_result, Data_memory_read_data, multiplexer_1_out,
       multiplexer_2_out, multiplexer_3_out, multiplexer_4_out, multiplexer_5_out, register_1_q,
       Registers_read_data_1, Registers_read_data_2;

  Clock clock_1 (.out(clock_1_out));
  Register #(.width(4)) register_1 (
    .D(multiplexer_4_out), .en(1'b1), .Q(register_1_q), .clk(clock_1_out));  // open: clr
  Adder #(.width(4)) adder_1 (.a(register_1_q), .b(4'b0001), .out(adder_1_out));  // open: cin, cout
  Instruction_memory Instruction_memory (.Read_address(register_1_q), .Instruction(out_1));
  Control Control (
    .Instruction(out_1[15:12]), .Alu_control(Control_alu_control), .Jump(Control_jump),
    .Branch(Control_branch), .MemWrite(Control_memwrite), .MemRead(Control_memread),
    .RegWrite(Control_regwrite), .MemToReg(Control_memtoreg), .AluSrc(Control_alusrc), .RegDst(Control_regdst));
  Multiplexer #(.width(4), .enable("false")) multiplexer_1 (
    .in0(out_1[7:4]), .in1(out_1[3:0]), .out(multiplexer_1_out), .sel(Control_regdst));
  Clock clock_2 (.out(clock_2_out));
  Registers Registers (
    .Clock(clock_2_out), .Read_register_1(out_1[11:8]), .Write_register(multiplexer_1_out),
    .RegWrite(Control_regwrite), .Read_register_2(out_1[7:4]), .Write_data(multiplexer_5_out),
    .Read_data_1(Registers_read_data_1), .Read_data_2(Registers_read_data_2));
  Adder #(.width(4)) adder_2 (.a(adder_1_out), .b(out_1[3:0]), .out(adder_2_out));  // open: cin, cout
  Multiplexer #(.width(4), .enable("false")) multiplexer_2 (
    .in0(Registers_read_data_2), .in1(out_1[3:0]), .out(multiplexer_2_out), .sel(Control_alusrc));
  Multiplexer #(.width(4), .enable("false")) multiplexer_3 (
    .in0(adder_1_out), .in1(adder_2_out), .out(multiplexer_3_out), .sel(and_1_out));
  and and_1 (and_1_out, ALU_zero, Control_branch);
  ALU ALU (
    .A(Registers_read_data_1), .B(multiplexer_2_out), .ALU_control(Control_alu_control), .Zero(ALU_zero),
    .Alu_result(ALU_alu_result));
  Multiplexer #(.width(4), .enable("false")) multiplexer_4 (
    .in0(multiplexer_3_out), .in1(out_1[3:0]), .out(multiplexer_4_out), .sel(Control_jump));
  Data_memory Data_memory (
    .Address(ALU_alu_result), .Write_data(Registers_read_data_2), .MemWrite(Control_memwrite),
    .Clock(clock_3_out), .MemRead(Control_memread), .Read_data(Data_memory_read_data));
  Multiplexer #(.width(4), .enable("false")) multiplexer_5 (
    .in0(ALU_alu_result), .in1(Data_memory_read_data), .out(multiplexer_5_out), .sel(Control_memtoreg));
  Clock clock_3 (.out(clock_3_out));

  // Notes on the sheet:
  //   RegDest
  //   Opcode
  //   rt
  //   rd
  //   rt
  //   rs
  //   RegWrite
  //   AluSrc
  //   Zero
  //   MemWrite
  //   Branch
  //   MemRead
  //   MemToReg
  //   Jump
endmodule

module ALU (
  input  [3:0] A,
  input  [3:0] B,
  input  [1:0] ALU_control,
  output Zero,
  output [3:0] Alu_result
);

  wire [3:0] adder_1_out, and_1_out, or_1_out, subtractor_1_out;

  Adder #(.width(4)) adder_1 (.a(A), .b(B), .out(adder_1_out));  // open: cin, cout
  Subtractor #(.width(4)) subtractor_1 (.a(A), .b(B), .out(subtractor_1_out));  // open: bin, bout
  assign or_1_out = A | B;  // OR_Gate or_1, 4 bits wide
  assign and_1_out = A & B;  // AND_Gate and_1, 4 bits wide
  Multiplexer #(.select(2), .width(4), .enable("false")) multiplexer_1 (
    .in0(adder_1_out), .in1(subtractor_1_out), .in2(or_1_out), .in3(and_1_out), .out(Alu_result),
    .sel(ALU_control));
  nor nor_1 (Zero, Alu_result[0], Alu_result[1], Alu_result[2], Alu_result[3]);
endmodule

module Registers (
  input  Clock,
  input  [3:0] Read_register_1,
  input  [3:0] Write_register,
  input  RegWrite,
  input  [3:0] Read_register_2,
  input  [3:0] Write_data,
  output [3:0] Read_data_1,
  output [3:0] Read_data_2
);

  wire demultiplexer_1_out1, demultiplexer_1_out2, demultiplexer_1_out3, demultiplexer_1_out4,
       demultiplexer_1_out5, demultiplexer_1_out6, demultiplexer_1_out7, demultiplexer_1_out8,
       demultiplexer_1_out9, demultiplexer_1_out10, demultiplexer_1_out11, demultiplexer_1_out12;
  wire [3:0] and_1_out, multiplexer_1_out, s0_q, s1_q, s2_q, s3_q, s4_q, sp_q, t0_q, t1_q, t2_q, t3_q, t4_q,
       t5_q, zero_q;

  Demultiplexer #(.select(4)) demultiplexer_1 (
    .out1(demultiplexer_1_out1), .out2(demultiplexer_1_out2), .out3(demultiplexer_1_out3),
    .out4(demultiplexer_1_out4), .out5(demultiplexer_1_out5), .out6(demultiplexer_1_out6),
    .out7(demultiplexer_1_out7), .out8(demultiplexer_1_out8), .out9(demultiplexer_1_out9),
    .out10(demultiplexer_1_out10), .out11(demultiplexer_1_out11), .out12(demultiplexer_1_out12),
    .sel(and_1_out));  // open: out0, out13, out14, out15, in, en
  assign and_1_out = Write_register & multiplexer_1_out;  // AND_Gate and_1, 4 bits wide
  Multiplexer #(.width(4)) multiplexer_1 (
    .in0(4'b0000), .in1(4'b1111), .out(multiplexer_1_out), .sel(RegWrite));  // open: en
  Register #(.width(4)) zero (.D(4'b0000), .en(1'b1), .Q(zero_q), .clk(Clock));  // open: clr
  Register #(.width(4)) t0 (.D(Write_data), .en(demultiplexer_1_out1), .Q(t0_q), .clk(Clock));  // open: clr
  Register #(.width(4)) t1 (.D(Write_data), .en(demultiplexer_1_out2), .Q(t1_q), .clk(Clock));  // open: clr
  Register #(.width(4)) t2 (.D(Write_data), .en(demultiplexer_1_out3), .Q(t2_q), .clk(Clock));  // open: clr
  Register #(.width(4)) t3 (.D(Write_data), .en(demultiplexer_1_out4), .Q(t3_q), .clk(Clock));  // open: clr
  Register #(.width(4)) t4 (.D(Write_data), .en(demultiplexer_1_out5), .Q(t4_q), .clk(Clock));  // open: clr
  Register #(.width(4)) t5 (.D(Write_data), .en(demultiplexer_1_out6), .Q(t5_q), .clk(Clock));  // open: clr
  Register #(.width(4)) s0 (.D(Write_data), .en(demultiplexer_1_out7), .Q(s0_q), .clk(Clock));  // open: clr
  Register #(.width(4)) s1 (.D(Write_data), .en(demultiplexer_1_out8), .Q(s1_q), .clk(Clock));  // open: clr
  Register #(.width(4)) s2 (.D(Write_data), .en(demultiplexer_1_out9), .Q(s2_q), .clk(Clock));  // open: clr
  Register #(.width(4)) s3 (.D(Write_data), .en(demultiplexer_1_out10), .Q(s3_q), .clk(Clock));  // open: clr
  Register #(.width(4)) s4 (.D(Write_data), .en(demultiplexer_1_out11), .Q(s4_q), .clk(Clock));  // open: clr
  Register #(.width(4)) sp (.D(Write_data), .en(demultiplexer_1_out12), .Q(sp_q), .clk(Clock));  // open: clr
  Multiplexer #(.select(4), .width(4), .enable("false")) multiplexer_2 (
    .in0(zero_q), .in1(t0_q), .in2(t1_q), .in3(t2_q), .in4(t3_q), .in5(t4_q), .in6(t5_q), .in7(s0_q),
    .in8(s1_q), .in9(s2_q), .in10(s3_q), .in11(s4_q), .in12(sp_q), .out(Read_data_1), .sel(Read_register_1));  // open: in13, in14, in15
  Multiplexer #(.select(4), .width(4), .enable("false")) multiplexer_3 (
    .in0(zero_q), .in1(t0_q), .in2(t1_q), .in3(t2_q), .in4(t3_q), .in5(t4_q), .in6(t5_q), .in7(s0_q),
    .in8(s1_q), .in9(s2_q), .in10(s3_q), .in11(s4_q), .in12(sp_q), .out(Read_data_2), .sel(Read_register_2));  // open: in13, in14, in15
endmodule

module ControlUnit (
  input  [3:0] in_1,
  output [3:0] out_2
);

  wire [15:0] rom_2_data;
  wire [15:4] rom_1_data;

  ROM #(.addrWidth(4), .dataWidth(16)) rom_1 (.addr(in_1), .data({rom_1_data, out_2}));  // open: sel
  ROM #(.addrWidth(4), .dataWidth(16)) rom_2 (.addr(rom_1_data[15:12]), .data(rom_2_data));  // open: sel

  // Notes on the sheet:
  //   contents of rom_1 (hex, n*v repeats v):
  //   1123
  //   contents of rom_2 (hex, n*v repeats v):
  //   0 240 241 240 241 242 1e0 242 243 243 4 110 9
endmodule

module Data_memory (
  input  [3:0] Address,
  input  [3:0] Write_data,
  input  MemWrite,
  input  MemRead,
  input  Clock,
  output [3:0] Read_data
);

  RAM #(.addrWidth(4), .dataWidth(4), .bus("separate")) ram_1 (
    .addr(Address), .din(Write_data), .data(Read_data), .str(MemWrite), .clk(Clock), .ld(MemRead));  // open: sel, clr
endmodule

module Control (
  input  [3:0] Instruction,
  output [1:0] Alu_control,
  output Jump,
  output Branch,
  output MemWrite,
  output MemRead,
  output RegWrite,
  output MemToReg,
  output AluSrc,
  output RegDst
);

  wire [15:10] rom_1_data;

  ROM #(.addrWidth(4), .dataWidth(16)) rom_1 (
    .addr(Instruction),
    .data({rom_1_data, RegDst, AluSrc, MemToReg, RegWrite, MemRead, MemWrite, Branch, Jump, Alu_control}));  // open: sel

  // Notes on the sheet:
  //   contents of rom_1 (hex, n*v repeats v):
  //   0 240 241 140 141 142 1e0 242 143 243 4 110 9
endmodule

module Instruction_memory (
  input  [3:0] Read_address,
  output [15:0] Instruction
);

  ROM #(.addrWidth(4), .dataWidth(16)) rom_1 (.addr(Read_address), .data(Instruction));  // open: sel

  // Notes on the sheet:
  //   contents of rom_1 (hex, n*v repeats v):
  //   0 3114 5225 9123 5348 1235 2455 4552 8448 7151 b050 6040 c212 a004 0 6c10
endmodule
